// Logisim project ass1.circ as structural Verilog: 1 circuit, main circuit main
module main (
  input  S,
  input  A,
  input  D,
  input  B,
  input  in_5,
  input  D_2,
  input  En,
  input  in_8,
  input  in_9,
  input  in_10,
  input  in_11,
  input  in_12,
  input  in_13,
  input  up_down,
  input  reset,
  output Q,
  output Y,
  output A0,
  output Q_2,
  output A1,
  output A2,
  output A3
);

  wire adder_1_cout, adder_1_out, adder_2_cout, adder_2_out, adder_3_cout, adder_3_out, adder_4_out,
       clock_1_out, clock_2_out, multiplexer_1_out, multiplexer_2_out, multiplexer_3_out, multiplexer_4_out,
       not_1_out, not_2_out;

  Multiplexer multiplexer_1 (.in0(in_8), .in1(in_9), .out(multiplexer_1_out), .sel(up_down));
  Multiplexer multiplexer_2 (.in0(in_10), .in1(in_11), .out(multiplexer_2_out), .sel(up_down));
  Multiplexer multiplexer_3 (.in0(in_12), .in1(in_13), .out(multiplexer_3_out), .sel(up_down));
  not not_1 (not_1_out, S);
  // Transmission_Gate transmission_1: pin names not known; wires that end beside it: A, not_1_out, S, Y
  // Transmission_Gate transmission_2: pin names not known; wires that end beside it: B, S, not_1_out, Y
  Adder #(.width(1)) adder_1 (.a(A0), .b(in_5), .out(adder_1_out), .cout(adder_1_cout));  // open: cin
  Adder #(.width(1)) adder_2 (
    .a(A1), .b(multiplexer_1_out), .out(adder_2_out), .cin(adder_1_cout), .cout(adder_2_cout));
  Adder #(.width(1)) adder_3 (
    .a(A2), .b(multiplexer_2_out), .out(adder_3_out), .cin(adder_2_cout), .cout(adder_3_cout));
  Adder #(.width(1)) adder_4 (.a(A3), .b(multiplexer_3_out), .out(adder_4_out), .cin(adder_3_cout));  // open: cout
  Clock clock_1 (.out(clock_1_out));
  D_Flip_Flop d_ff_1 (.D(adder_1_out), .clk(clock_1_out), .Q(A0), .reset(reset));  // open: Qn, preset
  D_Flip_Flop d_ff_2 (.D(adder_2_out), .clk(clock_1_out), .Q(A1), .reset(reset));  // open: Qn, preset
  D_Flip_Flop d_ff_3 (.D(adder_3_out), .clk(clock_1_out), .Q(A2), .reset(reset));  // open: Qn, preset
  D_Flip_Flop d_ff_4 (.D(adder_4_out), .clk(clock_1_out), .Q(A3), .reset(reset));  // open: Qn, preset
  Multiplexer multiplexer_4 (.in0(multiplexer_4_out), .in1(D), .out(multiplexer_4_out), .sel(clock_2_out));
  not not_2 (not_2_out, clock_2_out);
  Clock clock_2 (.out(clock_2_out));
  Multiplexer multiplexer_5 (.in0(Q_2), .in1(D_2), .out(Q_2), .sel(En));
  Multiplexer multiplexer_6 (.in0(Q), .in1(multiplexer_4_out), .out(Q), .sel(not_2_out));

  // Notes on the sheet:
  //   S'
  //   S
  //   S'
endmodule
